# Fritzing sketch blinker-attiny45 (saved by Fritzing 0.9.2b)
circuit board: 3.78243cm x 3.41977cm
breadboards: 1

parts:
  R1 = Trimmer Potentiometer [maximum_resistance=10kΩ package=THT]
  IC1 = ATtiny25/45/85 [package="8P3, 8-lead, 0.300\" Wide Body, PDIP"]

nets:
  N1: R1.leg1, IC1.GND
  N2: R1.wiper, IC1.(PCINT4/XTAL2/CLKO/OC1B/ADC2)_PB4
  N3: R1.leg2, IC1.VCC

custom parts:
  ATtiny25/45/85: ATtiny25/45/85 8-bit AVR Microcontroller
