# Fritzing sketch double_switch-darlington (saved by Fritzing 0.9.2b)
circuit board: 2.84481cm x 2.86092cm
circuit board: 2.84481cm x 2.86092cm
breadboards: 1

parts:
  Q6 = npn-Powertransistor [package="TO220 [THT]"]
  Q7 = npn-Powertransistor [package="TO220 [THT]"]
  Q8 = npn-Powertransistor [package="TO220 [THT]"]
  Q9 = pnp-Powertransistor [package="TO220 [THT]"]
  Q10 = pnp-Powertransistor [package="TO220 [THT]"]
  R10 = Resistor [tolerance=±5% resistance=1k package=THT]
  R11 = Resistor [tolerance=±5% resistance=1k package=THT]
  R12 = Resistor [tolerance=±5% resistance=1k package=THT]
  R13 = Resistor [tolerance=±5% resistance=1k package=THT]
  R14 = Resistor [tolerance=±5% resistance=1k package=THT]
  R15 = Resistor [tolerance=±5% resistance=100 package=THT]
  S2 = Toggle Switch [package=THT]
  R16 = Resistor [tolerance=±5% resistance=4.7 package=THT]
  R17 = Resistor [tolerance=±5% resistance=4.7 package=THT]

nets:
  N1: Q6.base, R14.Pin_1
  N2: Q6.collector, R11.Pin_1, R13.Pin_1, R15.Pin_1
  GND: Q6.emitter, Q7.emitter, Q8.emitter, S2.L1
  N3: Q7.base, R11.Pin_0
  N4: Q7.collector, R16.Pin_0
  N5: Q8.base, R12.Pin_1
  N6: Q8.collector, R17.Pin_0
  N7: Q9.base, R10.Pin_1
  N8: Q9.collector, R17.Pin_1
  5V: Q9.emitter, Q10.emitter, R15.Pin_0, S2.L2
  N9: Q10.base, R13.Pin_0
  N10: Q10.collector, R16.Pin_1
  N11: R10.Pin_0, R12.Pin_0, R14.Pin_0, S2.COM
